# Fritzing sketch rpi-lcd-menu (saved by Fritzing 0.9.5d)
breadboards: 1

parts:
  LCD1 = LCD screen
  Raspberry_Pi_1 = Raspberry Pi 3 [part_number=RPI-3-V1.2]
  LCM1602_IIC1 = LCM1602 IIC [part_number="LCM1602 IIC" chip_label="LCM1602 IIC" package="DIP (Dual Inline) [THT]"]
  S1 = SWITCH-MOMENTARY-2 [package=tactile-pth-12mm]
  S2 = SWITCH-MOMENTARY-2 [package=tactile-pth-12mm]
  S3 = SWITCH-MOMENTARY-2 [package=tactile-pth-12mm]
  S4 = SWITCH-MOMENTARY-2 [package=tactile-pth-12mm]
  R1 = Resistor [tolerance=±5% resistance=1k package="0402 [SMD]"]
  R2 = Resistor [tolerance=±5% resistance=1k package="0402 [SMD]"]
  R3 = Resistor [tolerance=±5% resistance=1k package="0402 [SMD]"]
  R4 = Resistor [tolerance=±5% resistance=1k package="0402 [SMD]"]

nets:
  VSS: LCD1.VSS, LCM1602_IIC1.VSS
  VDD: LCD1.VDD, LCM1602_IIC1.VDD
  N1: LCD1.V0, LCM1602_IIC1.V0
  N2: LCD1.RS, LCM1602_IIC1.RS
  N3: LCD1.R/W, LCM1602_IIC1.RW
  N4: LCD1.E, LCM1602_IIC1.E
  N5: LCD1.DB0, LCM1602_IIC1.D0
  N6: LCD1.DB1, LCM1602_IIC1.D1
  N7: LCD1.DB2, LCM1602_IIC1.D2
  N8: LCD1.DB3, LCM1602_IIC1.D3
  N9: LCD1.DB4, LCM1602_IIC1.D4
  N10: LCD1.DB5, LCM1602_IIC1.D5
  N11: LCD1.DB6, LCM1602_IIC1.D6
  N12: LCD1.DB7, LCM1602_IIC1.D7
  N13: LCD1.LED+, LCM1602_IIC1.A
  N14: LCD1.LED-, LCM1602_IIC1.K
  N15: Raspberry_Pi_1.GPIO2, LCM1602_IIC1.SDA
  N16: Raspberry_Pi_1.GPIO3, LCM1602_IIC1.SCL
  N17: Raspberry_Pi_1.GPIO4, R3.Pin_0
  N18: Raspberry_Pi_1.GPIO27, R1.Pin_0
  N19: Raspberry_Pi_1.GPIO5, R4.Pin_0
  N20: Raspberry_Pi_1.GPIO6, R2.Pin_0
  GND: Raspberry_Pi_1.GND, LCM1602_IIC1.GND, S1.2, S2.2, S3.2, S4.2
  5V: Raspberry_Pi_1.5V, LCM1602_IIC1.VCC
  N21: LCM1602_IIC1.LED_A, LCM1602_IIC1.LED_B
  N22: S1.1, R1.Pin_1
  N23: S2.1, R2.Pin_1
  N24: S3.1, R3.Pin_1
  N25: S4.1, R4.Pin_1

notes:
  Back
  Prev
  Next
  Apply

custom parts:
  LCM1602 IIC: I2C-Module to use a 1602 or 2004 LCD on with the wire.h libory Serial LCD Modul
